# Fritzing sketch schematic (saved by Fritzing 0.9.3b)
breadboards: 1

parts:
  R1 = Resistor [tolerance=±20% resistance=10k package=THT]
  Arduino = Arduino Uno (Rev3) - ICSP
  Hall_Sensor = mystery part, 3 pins [chip_label=?]

nets:
  N1: R1.Pin_0, Arduino.5V, Hall_Sensor.pin1
  N2: R1.Pin_1, Arduino.D2, Hall_Sensor.pin3
  N3: Arduino.GND, Hall_Sensor.pin2
